# Fritzing sketch i2c_devices (saved by Fritzing 0.8.7b)
breadboards: 2

parts:
  LCM1602_IIC1 = LCM1602 IIC [part_number="LCM1602 IIC" chip_label="LCM1602 IIC" package="DIP (Dual Inline) [THT]"]
  U1 = LCD-16X2 [package=lcd-16x2]
  Part1 = Triple Axis Accelerometer Breakout - ADXL345
  OLED_I2C1 = OLED 128x64 I2C Monochrome Display
  M1 = DOIT Esp32 DevKit v1 (30 pins long, 11 pins width) [part_number=ESP32S-PIN30]

nets:
  VSS: LCM1602_IIC1.VSS, LCM1602_IIC1.VDD, LCM1602_IIC1.V0, U1.VSS, U1.VDD, U1.VO
  N1: LCM1602_IIC1.RS, U1.RS
  N2: LCM1602_IIC1.RW, U1.R_W
  N3: LCM1602_IIC1.E, U1.E
  N4: LCM1602_IIC1.D0, U1.DB0
  N5: LCM1602_IIC1.D1, U1.DB1
  N6: LCM1602_IIC1.D2, U1.DB2
  N7: LCM1602_IIC1.D3, LCM1602_IIC1.D4, LCM1602_IIC1.D5, LCM1602_IIC1.D6, LCM1602_IIC1.D7, U1.DB3, U1.DB4, U1.DB5, U1.DB6, U1.DB7
  N8: LCM1602_IIC1.A, U1.A
  N9: LCM1602_IIC1.K, U1.K
  GND: LCM1602_IIC1.GND, Part1.GND, OLED_I2C1.GND, M1.GND
  VCC: LCM1602_IIC1.VCC, Part1.VCC, OLED_I2C1.VDD, M1.3V3
  N10: LCM1602_IIC1.SDA, Part1.SDA, OLED_I2C1.SDA, M1.D21
  N11: LCM1602_IIC1.SCL, Part1.SCL, OLED_I2C1.SCK, M1.D22

custom parts:
  LCM1602 IIC: I2C-Module to use a 1602 or 2004 LCD on with the wire.h libory Serial LCD Modul
  DOIT Esp32 DevKit v1 (30 pins long, 11 pins width): The DOIT Esp32 DevKit v1 is one of the development board created by DOIT to evaluate the ESP-WROOM-32 module. It is based on the ESP32 microcontroller that boasts Wifi, Bluetooth, Ethernet and Low Power support all in a single chip. (vanepp) made breadboard work, adjusted pin numbering and labels and reduced size of schematic and cleaned up pcb. This chip is 30pins long (2 x15) and 11 pins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
